// Logisim project lab3.circ as structural Verilog: 4 circuits, main circuit mux2to1
module mux2to1 (
  input  x,
  input  s,
  input  y,
  output m
);

  wire and_1_out, and_2_out, not_1_out;

  not not_1 (not_1_out, s);
  and and_1 (and_1_out, x, not_1_out);
  and and_2 (and_2_out, s, y);
  or or_1 (m, and_1_out, and_2_out);
endmodule

module demux1to2 (
  input  m,
  input  s,
  output x,
  output y
);

  wire not_1_out;

  not not_1 (not_1_out, s);
  and and_1 (x, m, not_1_out);
  and and_2 (y, s, m);
endmodule

module mux6to1 (
  input  input0,
  input  input1,
  input  input2,
  input  input3,
  input  input4,
  input  input5,
  input  s0,
  input  s1,
  input  s2,
  output output0
);

  wire mux2to1_1_m, mux2to1_2_m, mux2to1_3_m, mux2to1_4_m;

  mux2to1 mux2to1_1 (.x(input0), .s(s0), .y(input1), .m(mux2to1_1_m));
  mux2to1 mux2to1_2 (.x(input2), .s(s0), .y(input3), .m(mux2to1_2_m));
  mux2to1 mux2to1_3 (.x(input4), .s(s0), .y(input5), .m(mux2to1_3_m));
  mux2to1 mux2to1_4 (.x(mux2to1_1_m), .s(s1), .y(mux2to1_2_m), .m(mux2to1_4_m));
  mux2to1 mux2to1_5 (.x(mux2to1_4_m), .s(s2), .y(mux2to1_3_m), .m(output0));
endmodule

module demux1to6 (
  input  input0,
  input  s2,
  input  s1,
  input  s0,
  output output0,
  output output1,
  output output2,
  output output3,
  output output4,
  output output5
);

  wire demux1to2_1_x, demux1to2_1_y, demux1to2_2_x, demux1to2_2_y;

  demux1to2 demux1to2_1 (.m(input0), .s(s2), .x(demux1to2_1_x), .y(demux1to2_1_y));
  demux1to2 demux1to2_2 (.m(demux1to2_1_x), .s(s1), .x(demux1to2_2_x), .y(demux1to2_2_y));
  demux1to2 demux1to2_3 (.m(demux1to2_2_x), .s(s0), .x(output0), .y(output1));
  demux1to2 demux1to2_4 (.m(demux1to2_2_y), .s(s0), .x(output2), .y(output3));
  demux1to2 demux1to2_5 (.m(demux1to2_1_y), .s(s0), .x(output4), .y(output5));
endmodule
