// Logisim project lab4.circ as structural Verilog: 3 circuits, main circuit SR_Latch
module SR_Latch (
  input  S,
  input  C,
  input  R,
  output notQ,
  output Q
);

  wire and_1_out, and_2_out;

  and and_1 (and_1_out, S, C);
  and and_2 (and_2_out, C, R);
  nor nor_1 (notQ, and_1_out, Q);
  nor nor_2 (Q, notQ, and_2_out);
endmodule

module D_Latch (
  input  D,
  input  C,
  output notQ,
  output Q
);

  wire not_1_out;

  not not_1 (not_1_out, D);
  SR_Latch sr_latch_1 (.S(D), .C(C), .R(not_1_out), .notQ(notQ), .Q(Q));
endmodule

module D_Flip_Flop (
  input  D,
  input  C,
  output notQ,
  output Q
);

  wire d_latch_1_q, not_1_out, not_2_out;

  not not_1 (not_1_out, C);
  not not_2 (not_2_out, not_1_out);
  D_Latch d_latch_1 (.D(D), .C(not_1_out), .Q(d_latch_1_q));  // open: notQ
  D_Latch d_latch_2 (.D(d_latch_1_q), .C(not_2_out), .notQ(notQ), .Q(Q));
endmodule
