// Logisim project lab5.circ as structural Verilog: 1 circuit, main circuit the_Pen_Grenade
module the_Pen_Grenade (
  input  Click,
  input  Reset,
  output Armed
);

  wire and_1_out, and_2_out, and_3_out, and_4_out, and_5_out, and_6_out, and_7_out, F0_q, F0_qn, F1_q, F1_qn,
       F2_q, F2_qn, F3_q, F3_qn, or_1_out, or_2_out, or_3_out;

  D_Flip_Flop F3 (.D(or_1_out), .clk(Click), .Q(F3_q), .Qn(F3_qn), .reset(Reset));  // open: preset
  D_Flip_Flop F2 (.D(F1_q), .clk(Click), .Q(F2_q), .Qn(F2_qn), .reset(Reset));  // open: preset
  D_Flip_Flop F1 (.D(or_2_out), .clk(Click), .Q(F1_q), .Qn(F1_qn), .reset(Reset));  // open: preset
  D_Flip_Flop F0 (.D(or_3_out), .clk(Click), .Q(F0_q), .Qn(F0_qn), .reset(Reset));  // open: preset
  and and_1 (and_1_out, F3_q, F0_qn);
  and and_2 (and_2_out, F3_qn, F0_q);
  or or_1 (or_1_out, F2_q, and_1_out);
  and and_3 (and_3_out, F2_q, F0_q);
  or or_2 (or_2_out, and_3_out, and_2_out);
  and and_4 (and_4_out, F3_q, F2_q, F1_q);
  and and_5 (and_5_out, F2_qn, F0_qn);
  or or_3 (or_3_out, F3_qn, and_5_out);
  and and_6 (and_6_out, F3_q, F2_q, F1_qn, F0_qn);
  and and_7 (and_7_out, F2_qn, F3_q, F1_qn);
  or or_4 (Armed, and_4_out, and_6_out, and_7_out);
endmodule
