// Logisim project lab6.circ as structural Verilog: 1 circuit, main circuit main
module main (
  input  [3:0] file_input,
  input  [1:0] read_select,
  input  clock,
  input  enable,
  input  [1:0] write_select,
  output [3:0] file_output
);

  wire demultiplexer_1_out0, demultiplexer_1_out1, demultiplexer_1_out2, demultiplexer_1_out3;
  wire [3:0] register0_q, register1_q, register2_q, register3_q;

  Register #(.width(4)) register0 (
    .D(file_input), .en(demultiplexer_1_out0), .clk(clock), .Q(register0_q));  // open: clr
  Demultiplexer #(.enable("false"), .select(2)) demultiplexer_1 (
    .out0(demultiplexer_1_out0), .out1(demultiplexer_1_out1), .out2(demultiplexer_1_out2),
    .out3(demultiplexer_1_out3), .in(enable), .sel(write_select));
  Register #(.width(4)) register1 (
    .D(file_input), .en(demultiplexer_1_out1), .clk(clock), .Q(register1_q));  // open: clr
  Register #(.width(4)) register2 (
    .D(file_input), .en(demultiplexer_1_out2), .clk(clock), .Q(register2_q));  // open: clr
  Register #(.width(4)) register3 (
    .D(file_input), .en(demultiplexer_1_out3), .clk(clock), .Q(register3_q));  // open: clr
  Multiplexer #(.enable("false"), .select(2), .width(4)) multiplexer_1 (
    .in0(register0_q), .in1(register1_q), .in2(register2_q), .in3(register3_q), .out(file_output),
    .sel(read_select));
endmodule
